// Digital circuit MyAdder.dig as structural Verilog
module MyAdder (
  input  A,
  input  B,
  input  Cin,
  output out_sum,
  output Cout
);

  wire and_1_out, and_2_out, and_3_out, and_4_out, and_5_out, and_6_out, and_7_out, nand_1_out, or_1_out,
       or_2_out;

  and and_1 (and_1_out, A, B);
  nand nand_1 (nand_1_out, A, B);
  and and_2 (and_2_out, ~A, B);  // And
  and and_3 (and_3_out, A, ~B);  // And
  or or_1 (or_1_out, and_2_out, and_3_out);
  and and_4 (and_4_out, and_2_out, Cin);
  and and_5 (and_5_out, and_3_out, Cin);
  or or_2 (or_2_out, and_1_out, nand_1_out);
  and and_6 (and_6_out, or_2_out, Cin);
  and and_7 (and_7_out, Cin, or_1_out);
  or or_3 (Cout, and_4_out, A, and_5_out);
  or or_4 (out_sum, and_6_out, and_7_out);
endmodule
